# Fritzing sketch gemma (saved by Fritzing 0.9.2b)
breadboards: 1

parts:
  NEOPIXEL1 = Neopixel Strip -- Black (60/m)
  Part1 = Gemma
  U1 = LIPO-2000mAh [package=lipo-2000]
  S1 = Pushbutton [package=THT]

nets:
  GND: NEOPIXEL1.GND, Part1.GND, S1.leg1
  N1: NEOPIXEL1.DO, Part1.Vout
  N2: NEOPIXEL1.+5V#6, Part1.D1
  N3: Part1.D2, S1.leg0
  N4: U1.+, U1.-

notes:
  Zip con filo conduttivo

custom parts:
  Neopixel Strip -- Black (60/m): Neopixel Strip, Black, 60 pixels per meter.
  Gemma: GEMMA is a tiny wearable platform board with a lot of might in a 1" diameter package. Powered by a Attiny85 and programmable with an Arduino IDE over USB, you'll be able to realize any wearable project!
