# Fritzing sketch Test_Arduino (saved by Fritzing 0.9.2b)
breadboards: 1

parts:
  Part1 = Arduino Uno (Rev3)
  NEOPIXEL1 = Neopixel Strip -- Black (30/m)
  Power_plug1 = Power plug
  R1 = Resistor [tolerance=±5% resistance=470 package=THT]
  C1 = Electrolytic Capacitor [capacitance=10µF package="100 mil [THT, electrolytic]"]
  S1 = Pushbutton [package="[THT]"]
  R2 = Resistor [tolerance=±5% resistance=10k package=THT]

nets:
  GND: Part1.GND, NEOPIXEL1.GND, Power_plug1.GND, C1.-, R2.Pin_0
  N1: Part1.D2, S1.Pin_3, S1.Pin_4, R2.Pin_1
  N2: Part1.D6_PWM, R1.Pin_1
  N3: Part1.5V, S1.Pin_1, S1.Pin_2
  N4: NEOPIXEL1.Din, R1.Pin_0
  +5V: NEOPIXEL1.+5V, Power_plug1.VCC, C1.+

notes:
  Alimentazione NeoPixel
  In parallelo all'alimentazione

custom parts:
  Neopixel Strip -- Black (30/m): These NeoPixel strips have 30 digitally-addressable pixel LEDs per meter and are very affordable and are only 12.5 mm wide, 10 mm if you remove the strip from the casing.
