# Fritzing sketch pad (saved by Fritzing 0.9.3b)
breadboards: 1

parts:
  Pro_Micro1 = Pro Micro
  S1 = Pushbutton [package="[THT]"]
  S2 = Pushbutton [package="[THT]"]
  S3 = Pushbutton [package="[THT]"]
  S4 = Pushbutton [package="[THT]"]
  S5 = Pushbutton [package="[THT]"]
  S6 = Pushbutton [package="[THT]"]
  S7 = Pushbutton [package="[THT]"]
  S8 = Pushbutton [package="[THT]"]
  S9 = Pushbutton [package="[THT]"]
  S10 = Pushbutton [package="[THT]"]
  NEOPIXEL1 = Neopixel Strip -- Black (30/m) [part_number=1376]
  Power_plug1 = Power plug
  NEOPIXEL2 = Neopixel Strip -- Black (30/m) [part_number=1376]

nets:
  N1: Pro_Micro1.D7, S10.Pin_1, S10.Pin_2
  N2: Pro_Micro1.D8, S8.Pin_1, S8.Pin_2
  N3: Pro_Micro1.D9, NEOPIXEL2.Din
  N4: Pro_Micro1.D16/MOSI, S9.Pin_1, S9.Pin_2
  N5: S1.Pin_1, S1.Pin_2
  GND: S1.Pin_3, S1.Pin_4, S2.Pin_3, S2.Pin_4, S3.Pin_3, S3.Pin_4, S4.Pin_3, S4.Pin_4, S5.Pin_3, S5.Pin_4, S6.Pin_3, S6.Pin_4, S7.Pin_3, S7.Pin_4, S8.Pin_3, S8.Pin_4, S9.Pin_3, S9.Pin_4, S10.Pin_3, S10.Pin_4, NEOPIXEL1.GND, Power_plug1.GND, NEOPIXEL2.GND
  N6: S2.Pin_1, S2.Pin_2
  N7: S3.Pin_1, S3.Pin_2
  N8: S4.Pin_1, S4.Pin_2
  N9: S5.Pin_1, S5.Pin_2
  N10: S6.Pin_1, S6.Pin_2
  N11: S7.Pin_1, S7.Pin_2
  +5V: NEOPIXEL1.+5V, Power_plug1.VCC, NEOPIXEL2.+5V

notes:
  W
  S
  D
  Pads - Girls code it better 2017/18
  Code: https://goo.gl/UdFf25
  JUMP
  SX_M
  DOWN_M
  UP_M
  DX_M
  SX_B
  12V strip
  12V input
  A

custom parts:
  Pro Micro: The SparkFun Pro Micro is a complete USB-based microcontoller development system, in a very small footprint, capable of implementing many types of projects. All programming can be done via the USB port.
  Neopixel Strip -- Black (30/m): These NeoPixel strips have 30 digitally-addressable pixel LEDs per meter and are very affordable and are only 12.5 mm wide, 10 mm if you remove the strip from the casing.
