# Fritzing sketch Adafruit Feather HUZZAH (saved by Fritzing 0.9.3b)
breadboards: 1

parts:
  Part1 = Adafruit Feather HUZZAH ESP8266 [part_number="Adafruit #2821"]
  Part2 = Lithium Ion Polymer Battery 3.7v 150mAh [part_number=1317]  # not connected
  NEOPIXEL1 = Neopixel Strip -- Black (60/m)

nets:
  N1: Part1.CH_PD, Part1.GPIO2
  GND: Part1.GND, NEOPIXEL1.GND
  N2: Part1.VBAT, NEOPIXEL1.+5V
  N3: Part1.GPIO5/SCL, NEOPIXEL1.DI

notes:
  Davide Gariselli GCIB 2017
  3.7 Lipo Battery, no level converter needed

custom parts:
  Adafruit Feather HUZZAH ESP8266: his is the Adafruit Feather HUZZAH ESP8266 - our take on an 'all-in-one' ESP8266 WiFi development board with built in USB and battery charging. Its an ESP8266 WiFi module with all the extras you need, ready to rock! We have other boards in the Feather family, check'em out here. At the Feather HUZZAH's heart is an ESP8266 WiFi microcontroller clocked at 80 MHz and at 3.3V logic. This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
  Lithium Ion Polymer Battery 3.7v 150mAh: Lithium ion polymer (also known as 'lipo' or 'lipoly') batteries are thin, light and powerful. The output ranges from 4.2V when completely charged to 3.7V. This battery has a capacity of 150mAh for a total of about 0.6 Wh. The batteries come pre-attached with a genuine 2-pin JST-PH connector as shown and include the necessary protection circuitry.
  Neopixel Strip -- Black (60/m): Neopixel Strip, Black, 60 pixels per meter.
