# Fritzing sketch tacco_corno (saved by Fritzing 0.9.3b)
breadboards: 1

parts:
  R1 = Resistor [tolerance=±5% resistance=470 package=THT]  # not connected
  NEOPIXEL1 = Neopixel Strip -- Black (60/m)
  BB1 = 4-Line Bi-Directional Level Shifter
  U1 = NodeMCU V1.0

nets:
  N1: NEOPIXEL1.+5V, BB1.HV, U1.RSV
  N2: NEOPIXEL1.DI, BB1.B1
  GND: NEOPIXEL1.GND, BB1.GND, U1.GND
  N3: BB1.LV, U1.3V3
  N4: BB1.A1, U1.D5

notes:
  5V
  or VU

custom parts:
  Neopixel Strip -- Black (60/m): Neopixel Strip, Black, 60 pixels per meter.
  4-Line Bi-Directional Level Shifter: 4-Channel Bi-Directional Level Shifter
  NodeMCU V1.0: ESP8266 based NodeMCU
